# Fritzing sketch Doro-See (saved by Fritzing 0.9.3b)

parts:
  A1 = Raspberry Pi 5  # not connected
  부품1 = Arduino Uno (Rev3)
  Betain_BE-220 = bn-220- GPS-module
  J1 = Generic female header - 1 pins [form="♀ (female)" package=THT]
  USBTTL1 = USB A Plug
  USBTTL2 = Micro USB B Plug
  USBTTL3 = USB A Plug

nets:
  N1: 부품1.GND, Betain_BE-220.pin_1
  N2: 부품1.D3_PWM, Betain_BE-220.pin_3
  N3: 부품1.D4, Betain_BE-220.pin_2
  N4: 부품1.5V, Betain_BE-220.pin_4
  N5: J1.pin1, USBTTL1.usb
  N6: USBTTL2.usb, USBTTL3.usb

custom parts:
  Raspberry Pi 5: The RPi5, a faster version of the awesome Raspberry Pi4B ARM Board with 40 pin gpio.
  bn-220- GPS-module: bn-220l GPS module. Chipset : 8030-KT Receiving Format : GPS,GLONASS,Galileo,BeiDou,QZSS and SBAS
  Generic female header - 1 pins: Generic female header
